# Fritzing sketch FlightParameters (saved by Fritzing 0.9.3b)
breadboards: 2

parts:
  Part1 = Arduino Uno (Rev3)
  U1 = ESP8266 WiFi Module [part_number=ESP8266]
  Part2 = FTDI Basic Programmer
  LCD1 = LCD screen
  CONN1 = USB connector [package=THT]  # not connected
  U2 = Mini-USB _B_ connector with 5th pin broken out. [package=usb-minib]  # not connected
  R1 = TRIMPOT [package=trimpot-3mm]
  Part3 = Breadboard Power Supply Board SMD
  U3 = ESP8266 WiFi Module [part_number=ESP8266]
  R2 = Resistor [tolerance=±5% resistance=10k package=THT]
  R3 = Resistor [tolerance=±5% resistance=20k package=THT]
  GY1 = MPU-6050 Board GY-521 [form="♀ (female)" package=THT]  # not connected

nets:
  N1: Part1.D8, LCD1.E
  N2: Part1.D9_PWM, LCD1.RS
  N3: Part1.D10_PWM/SS, U3.TXD
  N4: Part1.D11_PWM/MOSI, R2.Pin_0
  GND: Part1.GND, LCD1.VSS, LCD1.R/W, LCD1.LED-, R1.CCW
  N5: Part1.D4, LCD1.DB7
  N6: Part1.D5_PWM, LCD1.DB6
  N7: Part1.D6_PWM, LCD1.DB5
  N8: Part1.D7, LCD1.DB4
  5V: Part1.5V, LCD1.VDD, LCD1.LED+, R1.CW
  N9: U1.RXD, Part2.TXO
  N10: U1.VCC, Part2.POWER
  GND_2: U1.GND, Part2.GND
  N11: U1.TXD, Part2.RXI
  N12: LCD1.V0, R1.WIPER
  GND_3: Part3.GND, Part3.VIN
  N13: U3.VCC, U3.CH_PD
  N14: U3.GPIO_0, U3.GND
  N15: R2.Pin_1, R3.Pin_0

notes:
  Connect breadboard power rails to get continuity.
  FTD232RL required for ESP8266 configuration via a computer. Not required when communicating with Arduino. External 3.3V recommended when with Arduino.
  Software Serial
  Pin 10 = RX, Pin 11 = TX
  3.3 V Supply for ESP8266
  3.3V
  GND
  TX
  RX
  TX from Ardunio needs to be stepped down from 5V to 3.3V RX for ESP8266. Connect a 10K and 20K in series and draw the V across the 20K.
  ESP8266 TX
  ESP8266 RX

custom parts:
  ESP8266 WiFi Module: Generic WiFi Module based on the ESP8266 with onboard PCB antenna and UART communications
  MPU-6050 Board GY-521: Acelerometro y Giroscopio MPU-6050 Board GY-521
